# Fritzing sketch scheme_CustomVariometer (saved by Fritzing 0.9.3b)
breadboards: 1

parts:
  Componente1 = Adafruit BMP280 [part_number="Adafruit #2651"]
  A1 = Esp32-c3 super mini
  Componente2 = OLED Monochrome 128x64 0.96 inch [part_number=326]
  J1 = Piezo Speaker

nets:
  GND: Componente1.GND, A1.Pin_15, Componente2.GND, J1.pin2
  N1: Componente1.SDI/SDA, A1.Pin_2
  N2: Componente1.SCK/SCL, A1.Pin_13
  N3: Componente1.3.3V, A1.Pin_14
  N4: Componente1.SDO/ADR, A1.Pin_1
  N5: Componente1.CS, A1.Pin_3
  N6: A1.Pin_4, Componente2.MOSI_SDA
  N7: A1.Pin_5, Componente2.SCLK_SCK
  N8: A1.Pin_12, J1.pin1
  N9: A1.Pin_16, Componente2.VIN

custom parts:
  Adafruit BMP280: Bosch has stepped up their game with their new BMP280 sensor, an environmental sensor with temperature, barometric pressure that is the next generation upgrade to the BMP085/BMP180/BMP183. This sensor is great for all sorts of weather sensing and can even be used in both I2C and SPI! This precision sensor from Bosch is the best low-cost, precision sensing solution for measuring barometric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
  Esp32-c3 super mini: ESP32-C3 Development Board ESP32 SuperMini Development Board ESP32 Development Board WiFi Bluetooth.
  OLED Monochrome 128x64 0.96 inch: These displays are small, only about 1" diameter, but very readable due to the high contrast of an OLED display. This display is made of 128x64 individual white OLED pixels, each one is turned on or off by the controller chip. Because the display makes its own light, no backlight is required. This reduces the power required to run the OLED and is why the display has such high contrast; we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
